// Logisim project PutyataMikhailAlexandrovich_lab1.circ as structural Verilog: 1 circuit, main circuit main
module main (
  input  in_1
);

  wire and_1_out, and_2_out, and_3_out, and_4_out, and_5_out, and_6_out, and_7_out, and_8_out, and_9_out,
       and_10_out, and_11_out, and_12_out, and_13_out, and_14_out, and_15_out, and_16_out, and_17_out,
       and_18_out, and_19_out, and_20_out, and_21_out, and_22_out, and_23_out, and_24_out, and_25_out,
       and_26_out, and_27_out, and_28_out, and_29_out, and_30_out, and_31_out, and_32_out, and_33_out,
       and_34_out, and_35_out, and_36_out, and_37_out, and_38_out, and_39_out, dipswitch_1_sw1,
       dipswitch_1_sw2, dipswitch_1_sw3, dipswitch_1_sw4, dipswitch_1_sw5, not_1_out, not_2_out, not_3_out,
       not_4_out, not_5_out, not_6_out, not_7_out, not_8_out, not_9_out, not_10_out, not_11_out, not_12_out,
       not_13_out, not_14_out, not_15_out, not_16_out, not_17_out, not_18_out, not_19_out, not_20_out,
       not_21_out, not_22_out, not_23_out, not_24_out, not_25_out, not_26_out, not_27_out, not_28_out,
       or_1_out, or_2_out, or_3_out, or_4_out, or_5_out, or_6_out, or_7_out, or_8_out, or_9_out, or_10_out,
       or_11_out, or_12_out, or_13_out, or_14_out, or_15_out, or_16_out, or_17_out, or_18_out, or_19_out,
       or_20_out, or_21_out;

  not not_1 (not_1_out, dipswitch_1_sw1);
  and and_1 (and_1_out, not_1_out, not_2_out);
  not not_2 (not_2_out, dipswitch_1_sw2);
  and and_2 (and_2_out, dipswitch_1_sw1, dipswitch_1_sw2);
  and and_3 (and_3_out, dipswitch_1_sw1, not_3_out);
  not not_3 (not_3_out, dipswitch_1_sw2);
  not not_4 (not_4_out, dipswitch_1_sw1);
  and and_4 (and_4_out, not_4_out, dipswitch_1_sw2);
  not not_5 (not_5_out, dipswitch_1_sw1);
  and and_5 (and_5_out, not_5_out, not_6_out);
  not not_6 (not_6_out, dipswitch_1_sw2);
  and and_6 (and_6_out, dipswitch_1_sw1, dipswitch_1_sw2);
  not not_7 (not_7_out, dipswitch_1_sw1);
  and and_7 (and_7_out, not_7_out, dipswitch_1_sw2);
  not not_8 (not_8_out, dipswitch_1_sw1);
  and and_8 (and_8_out, not_8_out, not_9_out);
  not not_9 (not_9_out, dipswitch_1_sw2);
  not not_10 (not_10_out, dipswitch_1_sw1);
  and and_9 (and_9_out, not_10_out, not_11_out);
  not not_11 (not_11_out, dipswitch_1_sw2);
  DipSwitch #(.number(5)) dipswitch_1 (
    .sw1(dipswitch_1_sw1), .sw2(dipswitch_1_sw2), .sw3(dipswitch_1_sw3), .sw4(dipswitch_1_sw4),
    .sw5(dipswitch_1_sw5));
  or or_1 (or_1_out, dipswitch_1_sw1, ~dipswitch_1_sw2, ~dipswitch_1_sw3, ~dipswitch_1_sw4, dipswitch_1_sw5);  // OR_Gate
  or or_2 (or_2_out, dipswitch_1_sw1, dipswitch_1_sw2, dipswitch_1_sw3, ~dipswitch_1_sw4, ~dipswitch_1_sw5);  // OR_Gate
  or or_3 (or_3_out, dipswitch_1_sw1, dipswitch_1_sw2, dipswitch_1_sw3, dipswitch_1_sw4, dipswitch_1_sw5);
  or or_4 (or_4_out, ~dipswitch_1_sw1, ~dipswitch_1_sw2, ~dipswitch_1_sw3, ~dipswitch_1_sw4, dipswitch_1_sw5);  // OR_Gate
  or or_5 (or_5_out, dipswitch_1_sw1, ~dipswitch_1_sw2, dipswitch_1_sw3, dipswitch_1_sw4, dipswitch_1_sw5);  // OR_Gate
  or or_6 (or_6_out, dipswitch_1_sw1, dipswitch_1_sw2, dipswitch_1_sw3, dipswitch_1_sw4, ~dipswitch_1_sw5);  // OR_Gate
  or or_7 (or_7_out, dipswitch_1_sw1, dipswitch_1_sw2, dipswitch_1_sw3, ~dipswitch_1_sw4, ~dipswitch_1_sw5);  // OR_Gate
  or or_8 (or_8_out, ~dipswitch_1_sw1, ~dipswitch_1_sw2, dipswitch_1_sw3, dipswitch_1_sw4, ~dipswitch_1_sw5);  // OR_Gate
  or or_9 (or_9_out, ~dipswitch_1_sw1, dipswitch_1_sw2, ~dipswitch_1_sw3, ~dipswitch_1_sw4, dipswitch_1_sw5);  // OR_Gate
  or or_10 (or_10_out, dipswitch_1_sw1, ~dipswitch_1_sw2, ~dipswitch_1_sw3, ~dipswitch_1_sw4, dipswitch_1_sw5);  // OR_Gate
  or or_11 (or_11_out, dipswitch_1_sw1, dipswitch_1_sw2, dipswitch_1_sw3, dipswitch_1_sw4, ~dipswitch_1_sw5);  // OR_Gate
  or or_12 (or_12_out, ~dipswitch_1_sw1, ~dipswitch_1_sw2, dipswitch_1_sw3, dipswitch_1_sw4, ~dipswitch_1_sw5);  // OR_Gate
  or or_13 (or_13_out, ~dipswitch_1_sw1, ~dipswitch_1_sw2, ~dipswitch_1_sw3, ~dipswitch_1_sw4, dipswitch_1_sw5);  // OR_Gate
  or or_14 (or_14_out, dipswitch_1_sw1, ~dipswitch_1_sw2, dipswitch_1_sw3, dipswitch_1_sw4, dipswitch_1_sw5);  // OR_Gate
  or or_15 (or_15_out, ~dipswitch_1_sw1, dipswitch_1_sw2, ~dipswitch_1_sw3, ~dipswitch_1_sw4, dipswitch_1_sw5);  // OR_Gate
  and and_10 (and_10_out, and_1_out, not_12_out);
  not not_12 (not_12_out, dipswitch_1_sw3);
  and and_11 (and_11_out, and_2_out, not_13_out);
  not not_13 (not_13_out, dipswitch_1_sw3);
  and and_12 (and_12_out, and_3_out, dipswitch_1_sw3);
  and and_13 (and_13_out, and_4_out, dipswitch_1_sw3);
  and and_14 (and_14_out, and_5_out, not_14_out);
  not not_14 (not_14_out, dipswitch_1_sw3);
  and and_15 (and_15_out, and_6_out, dipswitch_1_sw3);
  and and_16 (and_16_out, and_7_out, not_15_out);
  not not_15 (not_15_out, dipswitch_1_sw3);
  and and_17 (and_17_out, and_8_out, not_16_out);
  not not_16 (not_16_out, dipswitch_1_sw3);
  and and_18 (and_18_out, and_9_out, not_17_out);
  not not_17 (not_17_out, dipswitch_1_sw3);
  LedBar #(.matrixcols(3)) ledbar_1 (.led0(or_20_out), .led1(or_21_out), .led2(or_19_out));
  LedBar #(.matrixcols(3)) ledbar_2 (.led0(and_19_out), .led1(and_20_out), .led2(and_21_out));
  and and_19 (and_19_out, or_1_out, or_2_out, or_3_out, or_4_out, or_5_out);
  and and_20 (and_20_out, or_6_out, or_7_out, or_8_out, or_9_out);
  and and_21 (and_21_out, or_10_out, or_11_out, or_12_out, or_13_out, or_14_out, or_15_out);
  and and_22 (and_22_out, and_10_out, not_18_out);
  not not_18 (not_18_out, dipswitch_1_sw4);
  and and_23 (and_23_out, and_11_out, not_19_out);
  not not_19 (not_19_out, dipswitch_1_sw4);
  and and_24 (and_24_out, and_12_out, dipswitch_1_sw4);
  not not_20 (not_20_out, dipswitch_1_sw5);
  and and_25 (and_25_out, and_13_out, dipswitch_1_sw4);
  not not_21 (not_21_out, dipswitch_1_sw5);
  and and_26 (and_26_out, and_14_out, not_22_out);
  not not_22 (not_22_out, dipswitch_1_sw4);
  not not_23 (not_23_out, dipswitch_1_sw5);
  and and_27 (and_27_out, and_15_out, dipswitch_1_sw4);
  not not_24 (not_24_out, dipswitch_1_sw5);
  and and_28 (and_28_out, and_16_out, not_25_out);
  not not_25 (not_25_out, dipswitch_1_sw4);
  not not_26 (not_26_out, dipswitch_1_sw5);
  and and_29 (and_29_out, and_17_out, dipswitch_1_sw4);
  and and_30 (and_30_out, and_18_out, not_27_out);
  not not_27 (not_27_out, dipswitch_1_sw4);
  not not_28 (not_28_out, dipswitch_1_sw5);
  and and_31 (and_31_out, and_22_out, dipswitch_1_sw5);
  and and_32 (and_32_out, and_23_out, dipswitch_1_sw5);
  and and_33 (and_33_out, and_24_out, not_20_out);
  and and_34 (and_34_out, and_25_out, not_21_out);
  and and_35 (and_35_out, and_26_out, not_23_out);
  and and_36 (and_36_out, and_27_out, not_24_out);
  and and_37 (and_37_out, and_28_out, not_26_out);
  and and_38 (and_38_out, and_29_out, dipswitch_1_sw5);
  and and_39 (and_39_out, and_30_out, not_28_out);
  or or_16 (or_16_out, and_32_out, and_33_out);
  or or_17 (or_17_out, and_34_out, and_35_out);
  or or_18 (or_18_out, and_36_out, and_37_out);
  or or_19 (or_19_out, and_38_out, and_39_out);
  or or_20 (or_20_out, and_31_out, or_16_out);
  or or_21 (or_21_out, or_17_out, or_18_out);
endmodule
