// Logisim project PutyataMikhailAlexandrovich_lab2.circ as structural Verilog: 1 circuit, main circuit main
module main (
  input  Writing,
  input  [7:0] Adress,
  input  [19:0] Message,
  output [5:0] D1,
  output [5:0] D2,
  output [5:0] D3,
  output [5:0] D4,
  output [5:0] D5,
  output [2:0] out_9,
  output [5:0] M4,
  output [5:0] M3,
  output [5:0] M2,
  output [5:0] M1,
  output [5:0] R
);

  wire clock_1_out;
  wire [4:0] adder_1_out, adder_2_out;
  wire [5:5] adder_1_cout, adder_2_cout;
  wire [7:0] divider_1_rem;

  Clock clock_1 (.out(clock_1_out));
  assign M4 = {{1{1'b0}}, Message[4:0]};  // Bit_Extender bit_extender_1
  assign M3 = {{1{1'b0}}, Message[9:5]};  // Bit_Extender bit_extender_2
  assign M2 = {{1{1'b0}}, Message[14:10]};  // Bit_Extender bit_extender_3
  assign M1 = {{1{1'b0}}, Message[19:15]};  // Bit_Extender bit_extender_4
  Adder #(.width(5)) adder_1 (
    .a(Message[4:0]), .b(Message[14:10]), .out(adder_1_out), .cout(adder_1_cout[5]));  // open: cin
  Adder #(.width(5)) adder_2 (
    .a(Message[9:5]), .b(Message[19:15]), .out(adder_2_out), .cout(adder_2_cout[5]));  // open: cin
  assign R = {adder_1_cout[5], adder_1_out} ^ {adder_2_cout[5], adder_2_out};  // XOR_Gate xor_1, 6 bits wide
  Bit_Extender #(.out_width(3), .\type ("zero")) bit_extender_5 (.in(divider_1_rem), .out(out_9));
  Divider divider_1 (.a(Adress), .b(8'h5), .rem(divider_1_rem));  // open: out, upper
  Demultiplexer #(.select(3), .tristate("true"), .width(6)) demultiplexer_1 (
    .out0(D5), .out1(D5), .out2(D5), .out3(D5), .out4(D4), .in(M4), .sel(out_9));  // open: out5, out6, out7
  Demultiplexer #(.select(3), .tristate("true"), .width(6)) demultiplexer_2 (
    .out0(D4), .out1(D4), .out2(D4), .out3(D3), .out4(D3), .in(M3), .sel(out_9));  // open: out5, out6, out7
  Demultiplexer #(.select(3), .tristate("true"), .width(6)) demultiplexer_3 (
    .out0(D3), .out1(D3), .out2(D2), .out3(D2), .out4(D2), .in(M2), .sel(out_9));  // open: out5, out6, out7
  Demultiplexer #(.select(3), .tristate("true"), .width(6)) demultiplexer_4 (
    .out0(D2), .out1(D1), .out2(D1), .out3(D1), .out4(D1), .in(M1), .sel(out_9));  // open: out5, out6, out7
  Demultiplexer #(.select(3), .tristate("true"), .width(6)) demultiplexer_5 (
    .out0(D1), .out1(D2), .out2(D3), .out3(D4), .out4(D5), .in(R), .sel(out_9));  // open: out5, out6, out7
  RAM #(.dataWidth(6)) ram_1 (.addr(Adress), .we(Writing), .clk(clock_1_out), .din(D1));  // open: oe, dout
  RAM #(.dataWidth(6)) ram_2 (.addr(Adress), .we(Writing), .clk(clock_1_out), .din(D2));  // open: oe, dout
  RAM #(.dataWidth(6)) ram_3 (.addr(Adress), .we(Writing), .clk(clock_1_out), .din(D3));  // open: oe, dout
  RAM #(.dataWidth(6)) ram_4 (.addr(Adress), .we(Writing), .clk(clock_1_out), .din(D4));  // open: oe, dout
  RAM #(.dataWidth(6)) ram_5 (.addr(Adress), .we(Writing), .clk(clock_1_out), .din(D5));  // open: oe, dout
endmodule
