// Logisim project PutyataMikhailAlexandrovich_lab3_part1.circ as structural Verilog: 1 circuit, main circuit main
module main (
  input  in_1,
  input  [7:0] in_2,
  output out_3,
  output out_4,
  output [31:0] out_5,
  output out_6,
  output out_7,
  output out_8,
  output out_9,
  output out_10,
  output out_11,
  output [31:0] out_12
);

  wire and_1_out, and_2_out, and_3_out, and_4_out, and_5_out, and_6_out, and_7_out, and_8_out, and_9_out,
       clock_1_out, comparator_1_eq, comparator_2_eq, comparator_3_eq, comparator_4_eq, comparator_5_eq,
       comparator_6_eq, comparator_7_eq, comparator_8_eq, decoder_1_out0, decoder_1_out1, decoder_1_out2,
       decoder_1_out3, decoder_1_out4, decoder_1_out5, decoder_1_out6, decoder_1_out7, nor_1_out,
       register_18_q, register_19_q, register_20_q, register_21_q, register_22_q, register_23_q,
       register_24_q, register_25_q;
  wire [2:0] register_10_q, register_11_q, register_12_q, register_13_q, register_14_q, register_15_q,
       register_16_q, register_17_q;
  wire [7:0] multiplexer_1_out;
  wire [31:0] multiplexer_2_out, register_2_q, register_3_q, register_4_q, register_5_q, register_6_q,
       register_7_q, register_8_q, register_9_q;

  Clock clock_1 (.out(clock_1_out));
  RAM #(.addrWidth(6), .dataWidth(32)) ram_1 (.addr(in_2[7:2]), .clk(and_1_out), .dout(out_5));  // open: we, oe, din
  and and_1 (and_1_out, clock_1_out, nor_1_out);
  Register #(.trigger("falling")) register_1 (.D(multiplexer_1_out), .clk(clock_1_out));  // open: en, Q, clr
  Multiplexer #(.select(2), .width(8)) multiplexer_1 (
    .in0(out_12[7:0]), .in1(out_12[15:8]), .in2(out_12[23:16]), .in3(out_12[31:24]), .out(multiplexer_1_out),
    .sel(in_2[1:0]));
  Decoder #(.select(3)) decoder_1 (
    .out0(decoder_1_out0), .out1(decoder_1_out1), .out2(decoder_1_out2), .out3(decoder_1_out3),
    .out4(decoder_1_out4), .out5(decoder_1_out5), .out6(decoder_1_out6), .out7(decoder_1_out7),
    .sel(in_2[4:2]));  // open: en
  Register #(.trigger("falling"), .width(32)) register_2 (
    .D(out_5), .en(decoder_1_out7), .Q(register_2_q), .clk(and_1_out), .clr(in_1));
  Register #(.trigger("falling"), .width(32)) register_3 (
    .D(out_5), .en(decoder_1_out6), .Q(register_3_q), .clk(and_1_out), .clr(in_1));
  Register #(.trigger("falling"), .width(32)) register_4 (
    .D(out_5), .en(decoder_1_out5), .Q(register_4_q), .clk(and_1_out), .clr(in_1));
  Register #(.trigger("falling"), .width(32)) register_5 (
    .D(out_5), .en(decoder_1_out4), .Q(register_5_q), .clk(and_1_out), .clr(in_1));
  Register #(.trigger("falling"), .width(32)) register_6 (
    .D(out_5), .en(decoder_1_out3), .Q(register_6_q), .clk(and_1_out), .clr(in_1));
  Register #(.trigger("falling"), .width(32)) register_7 (
    .D(out_5), .en(decoder_1_out2), .Q(register_7_q), .clk(and_1_out), .clr(in_1));
  Register #(.trigger("falling"), .width(32)) register_8 (
    .D(out_5), .en(decoder_1_out1), .Q(register_8_q), .clk(and_1_out), .clr(in_1));
  Register #(.trigger("falling"), .width(32)) register_9 (
    .D(out_5), .en(decoder_1_out0), .Q(register_9_q), .clk(and_1_out), .clr(in_1));
  Register #(.trigger("falling"), .width(3)) register_10 (
    .D(in_2[7:5]), .en(decoder_1_out7), .Q(register_10_q), .clk(and_1_out), .clr(in_1));
  Register #(.trigger("falling"), .width(3)) register_11 (
    .D(in_2[7:5]), .en(decoder_1_out6), .Q(register_11_q), .clk(and_1_out), .clr(in_1));
  Register #(.trigger("falling"), .width(3)) register_12 (
    .D(in_2[7:5]), .en(decoder_1_out5), .Q(register_12_q), .clk(and_1_out), .clr(in_1));
  Register #(.trigger("falling"), .width(3)) register_13 (
    .D(in_2[7:5]), .en(decoder_1_out4), .Q(register_13_q), .clk(and_1_out), .clr(in_1));
  Register #(.trigger("falling"), .width(3)) register_14 (
    .D(in_2[7:5]), .en(decoder_1_out3), .Q(register_14_q), .clk(and_1_out), .clr(in_1));
  Register #(.trigger("falling"), .width(3)) register_15 (
    .D(in_2[7:5]), .en(decoder_1_out2), .Q(register_15_q), .clk(and_1_out), .clr(in_1));
  Register #(.trigger("falling"), .width(3)) register_16 (
    .D(in_2[7:5]), .en(decoder_1_out1), .Q(register_16_q), .clk(and_1_out), .clr(in_1));
  Register #(.trigger("falling"), .width(3)) register_17 (
    .D(in_2[7:5]), .en(decoder_1_out0), .Q(register_17_q), .clk(and_1_out), .clr(in_1));
  and and_2 (and_2_out, decoder_1_out7, and_1_out);
  and and_3 (and_3_out, decoder_1_out6, and_1_out);
  and and_4 (and_4_out, decoder_1_out5, and_1_out);
  and and_5 (and_5_out, decoder_1_out4, and_1_out);
  and and_6 (and_6_out, decoder_1_out3, and_1_out);
  and and_7 (and_7_out, decoder_1_out2, and_1_out);
  and and_8 (and_8_out, decoder_1_out1, and_1_out);
  and and_9 (and_9_out, decoder_1_out0, and_1_out);
  Register #(.trigger("falling"), .width(1)) register_18 (
    .D(and_2_out), .en(and_2_out), .Q(register_18_q), .clk(and_1_out), .clr(in_1));
  Register #(.trigger("falling"), .width(1)) register_19 (
    .D(and_3_out), .en(and_3_out), .Q(register_19_q), .clk(and_1_out), .clr(in_1));
  Register #(.trigger("falling"), .width(1)) register_20 (
    .D(and_4_out), .en(and_4_out), .Q(register_20_q), .clk(and_1_out), .clr(in_1));
  Register #(.trigger("falling"), .width(1)) register_21 (
    .D(and_5_out), .en(and_5_out), .Q(register_21_q), .clk(and_1_out), .clr(in_1));
  Register #(.trigger("falling"), .width(1)) register_22 (
    .D(and_6_out), .en(and_6_out), .Q(register_22_q), .clk(and_1_out), .clr(in_1));
  Register #(.trigger("falling"), .width(1)) register_23 (
    .D(and_7_out), .en(and_7_out), .Q(register_23_q), .clk(and_1_out), .clr(in_1));
  Register #(.trigger("falling"), .width(1)) register_24 (
    .D(and_8_out), .en(and_8_out), .Q(register_24_q), .clk(and_1_out), .clr(in_1));
  Register #(.trigger("falling"), .width(1)) register_25 (
    .D(and_9_out), .en(and_9_out), .Q(register_25_q), .clk(and_1_out), .clr(in_1));
  Comparator #(.mode("unsigned"), .width(3)) comparator_1 (
    .a(register_10_q), .b(in_2[7:5]), .eq(comparator_1_eq));  // open: gt, lt
  Comparator #(.mode("unsigned"), .width(3)) comparator_2 (
    .a(register_11_q), .b(in_2[7:5]), .eq(comparator_2_eq));  // open: gt, lt
  Comparator #(.mode("unsigned"), .width(3)) comparator_3 (
    .a(register_12_q), .b(in_2[7:5]), .eq(comparator_3_eq));  // open: gt, lt
  Comparator #(.mode("unsigned"), .width(3)) comparator_4 (
    .a(register_13_q), .b(in_2[7:5]), .eq(comparator_4_eq));  // open: gt, lt
  Comparator #(.mode("unsigned"), .width(3)) comparator_5 (
    .a(register_14_q), .b(in_2[7:5]), .eq(comparator_5_eq));  // open: gt, lt
  Comparator #(.mode("unsigned"), .width(3)) comparator_6 (
    .a(register_15_q), .b(in_2[7:5]), .eq(comparator_6_eq));  // open: gt, lt
  Comparator #(.mode("unsigned"), .width(3)) comparator_7 (
    .a(register_16_q), .b(in_2[7:5]), .eq(comparator_7_eq));  // open: gt, lt
  Comparator #(.mode("unsigned"), .width(3)) comparator_8 (
    .a(register_17_q), .b(in_2[7:5]), .eq(comparator_8_eq));  // open: gt, lt
  and and_10 (out_3, comparator_1_eq, register_18_q, decoder_1_out7);
  and and_11 (out_4, comparator_2_eq, register_19_q, decoder_1_out6);
  and and_12 (out_6, comparator_3_eq, register_20_q, decoder_1_out5);
  and and_13 (out_7, comparator_4_eq, register_21_q, decoder_1_out4);
  and and_14 (out_8, comparator_5_eq, register_22_q, decoder_1_out3);
  and and_15 (out_9, comparator_6_eq, register_23_q, decoder_1_out2);
  and and_16 (out_10, comparator_7_eq, register_24_q, decoder_1_out1);
  and and_17 (out_11, comparator_8_eq, register_25_q, decoder_1_out0);
  Multiplexer #(.select(3), .width(32)) multiplexer_2 (
    .in0(register_9_q), .in1(register_8_q), .in2(register_7_q), .in3(register_6_q), .in4(register_5_q),
    .in5(register_4_q), .in6(register_3_q), .in7(register_2_q), .out(multiplexer_2_out), .sel(in_2[4:2]));
  nor nor_1 (nor_1_out, out_3, out_4, out_6, out_7, out_8, out_9, out_10, out_11);
  Multiplexer #(.width(32)) multiplexer_3 (.in0(multiplexer_2_out), .in1(out_5), .out(out_12), .sel(nor_1_out));
endmodule
